// Logisim project 8-bit-computer.circ as structural Verilog: 1 circuit, main circuit main
module main (
  input  POWER,
  input  in_2,
  input  in_3,
  input  in_4,
  input  in_5,
  input  in_6,
  input  in_7,
  input  in_8,
  input  in_9,
  output out_10,
  output out_11,
  output out_12,
  output out_13,
  output out_14,
  output out_15,
  output out_16,
  output out_17
);

  wire A_in, A_out, ALU_op0, ALU_op1, ALU_out, and_1_out, and_2_out, and_3_out, and_4_out, and_5_out,
       and_6_out, and_7_out, and_8_out, and_9_out, and_10_out, and_11_out, and_12_out, and_13_out,
       and_14_out, and_15_out, and_16_out, and_17_out, and_18_out, and_19_out, and_20_out, and_21_out,
       and_22_out, and_23_out, and_24_out, and_25_out, and_26_out, and_27_out, and_28_out, and_29_out,
       and_30_out, and_31_out, and_32_out, and_33_out, and_34_out, and_35_out, and_36_out, and_37_out,
       and_38_out, and_39_out, and_40_out, and_41_out, and_42_out, and_43_out, and_44_out, and_45_out,
       and_46_out, and_47_out, and_48_out, and_49_out, and_50_out, and_51_out, and_52_out, and_53_out,
       and_54_out, and_55_out, and_56_out, and_57_out, and_58_out, and_59_out, and_60_out, and_61_out,
       and_62_out, and_63_out, and_64_out, and_65_out, and_66_out, and_67_out, and_68_out, and_69_out,
       and_70_out, and_71_out, and_72_out, and_73_out, and_74_out, and_75_out, and_76_out, and_77_out,
       and_78_out, and_79_out, and_80_out, and_81_out, and_82_out, and_83_out, and_84_out, and_85_out,
       and_86_out, and_87_out, and_88_out, and_89_out, and_90_out, and_91_out, and_92_out, and_93_out,
       and_94_out, and_95_out, and_96_out, and_97_out, and_98_out, and_99_out, and_100_out, and_101_out,
       and_102_out, and_103_out, and_104_out, and_105_out, and_106_out, and_107_out, and_108_out,
       and_109_out, and_110_out, and_111_out, and_112_out, and_113_out, and_114_out, and_115_out,
       and_116_out, and_117_out, and_118_out, and_119_out, and_120_out, and_121_out, and_122_out,
       and_123_out, and_124_out, and_125_out, and_126_out, and_127_out, and_128_out, and_129_out,
       and_130_out, and_131_out, and_132_out, and_133_out, and_134_out, and_135_out, and_136_out,
       and_137_out, and_138_out, and_139_out, and_140_out, and_141_out, and_142_out, and_143_out,
       and_144_out, and_145_out, and_146_out, and_147_out, and_148_out, and_149_out, and_150_out,
       and_151_out, and_152_out, and_153_out, and_154_out, and_155_out, and_156_out, and_157_out,
       and_158_out, and_159_out, and_160_out, and_161_out, and_162_out, and_163_out, and_164_out,
       and_165_out, and_166_out, and_167_out, and_168_out, and_169_out, and_170_out, and_171_out,
       and_172_out, and_173_out, and_174_out, and_175_out, and_176_out, and_177_out, and_178_out,
       and_179_out, and_180_out, and_181_out, and_182_out, and_183_out, and_184_out, and_185_out,
       and_186_out, and_187_out, and_188_out, B_in, B_out, button_1_out, C_in, C_out, Clock_out, HLT, IR_in,
       JCH, JCL, JZH, JZL, MARH_in, MARL_in, MEM_out, nand_1_out, nand_2_out, nand_3_out, nand_4_out,
       nand_5_out, nand_6_out, nand_7_out, nand_8_out, nand_9_out, not_1_out, not_2_out, not_3_out,
       not_4_out, not_5_out, not_6_out, not_7_out, not_8_out, not_9_out, not_10_out, not_11_out, not_12_out,
       not_13_out, not_14_out, not_15_out, not_16_out, not_17_out, not_18_out, not_19_out, not_20_out,
       not_21_out, not_22_out, not_23_out, not_24_out, not_25_out, not_26_out, not_27_out, not_28_out,
       not_29_out, not_30_out, not_31_out, or_1_out, or_2_out, or_4_out, or_5_out, or_7_out, or_8_out,
       or_10_out, or_11_out, or_13_out, or_14_out, or_16_out, or_17_out, or_19_out, or_20_out, or_22_out,
       or_23_out, or_25_out, or_26_out, or_27_out, or_28_out, or_29_out, or_30_out, or_31_out, or_32_out,
       or_33_out, or_34_out, or_35_out, or_36_out, or_37_out, or_38_out, or_39_out, or_40_out, or_41_out,
       or_42_out, or_43_out, or_44_out, or_45_out, or_46_out, or_47_out, or_48_out, or_49_out, or_50_out,
       or_51_out, or_52_out, or_53_out, or_54_out, or_55_out, or_56_out, or_57_out, or_58_out, or_59_out,
       or_60_out, or_61_out, or_62_out, or_63_out, or_64_out, or_65_out, or_66_out, or_67_out, or_68_out,
       or_69_out, or_70_out, or_71_out, or_72_out, or_73_out, or_74_out, or_75_out, or_76_out, or_77_out,
       or_78_out, or_79_out, or_80_out, or_81_out, or_82_out, or_83_out, or_84_out, or_85_out, or_86_out,
       or_87_out, or_88_out, or_89_out, or_90_out, or_91_out, or_92_out, or_93_out, or_94_out, or_95_out,
       or_96_out, or_97_out, or_98_out, or_99_out, or_100_out, or_101_out, or_102_out, or_103_out,
       or_104_out, or_105_out, or_106_out, or_107_out, or_108_out, or_109_out, or_110_out, or_111_out,
       or_112_out, or_113_out, or_114_out, or_115_out, or_116_out, or_117_out, or_118_out, or_119_out,
       or_120_out, or_121_out, or_122_out, or_123_out, or_124_out, or_125_out, or_126_out, or_127_out,
       or_128_out, or_129_out, or_130_out, OUT_in, PCH_in, PCH_out, PCH_write, PCL_in, PCL_out, PCL_write,
       RAM_in, RAM_out, register_13_q, register_14_q, register_15_q, register_16_q, register_17_q,
       register_18_q, register_19_q, register_20_q, register_37_q, register_38_q, register_39_q,
       register_40_q, register_41_q, register_42_q, register_43_q, register_44_q, register_45_q,
       register_46_q, register_47_q, register_48_q, register_49_q, register_50_q, register_51_q,
       register_52_q, register_53_q, Reset_Counter, SIGNED_data, SIGNED_in, xor_1_out, xor_2_out, xor_3_out,
       xor_4_out, xor_5_out, xor_6_out, xor_7_out, xor_8_out, xor_9_out, xor_10_out, xor_11_out, xor_12_out,
       xor_13_out, xor_14_out, xor_15_out, xor_16_out, xor_17_out, xor_18_out, xor_19_out, xor_20_out,
       xor_21_out, xor_22_out, xor_23_out, xor_24_out, xor_25_out, xor_26_out, xor_27_out, xor_28_out,
       xor_29_out, xor_30_out, xor_31_out, xor_32_out, xor_33_out, xor_34_out, xor_35_out, xor_36_out,
       xor_37_out, xor_38_out, xor_39_out, xor_40_out, xor_41_out, xor_42_out, xor_43_out, xor_44_out,
       xor_45_out, xor_46_out, xor_47_out, xor_48_out, xor_49_out, xor_50_out, xor_51_out, xor_52_out,
       xor_53_out, xor_54_out;
  wire [7:0] ram_1_data, rom_5_data, rom_6_data, rom_7_data, rom_8_data;
  wire [7:6] rom_4_data;
  wire [8:0] register_54_q;
  wire [11:0] register_1_q;
  wire [14:0] register_63_q;
  wire [15:0] register_21_q;

  Clock Clock (.out(Clock_out));
  and and_1 (and_1_out, POWER, Clock_out);
  not not_1 (not_1_out, HLT);
  Register #(.width(1)) register_1 (.D(not_2_out), .en(1'b1), .Q(register_1_q[0]), .clk(nand_1_out), .clr(or_1_out));
  Register #(.width(1)) register_2 (.D(xor_1_out), .en(1'b1), .Q(register_1_q[1]), .clk(nand_1_out), .clr(or_1_out));
  nand nand_1 (nand_1_out, and_1_out, not_1_out);
  Register #(.width(1)) register_3 (.D(xor_2_out), .en(1'b1), .Q(register_1_q[2]), .clk(nand_1_out), .clr(or_1_out));
  Register #(.width(1)) register_4 (.D(xor_3_out), .en(1'b1), .Q(register_1_q[3]), .clk(nand_1_out), .clr(or_1_out));
  Register #(.width(1)) register_5 (.D(out_17), .en(IR_in), .Q(register_1_q[4]), .clk(nand_1_out));  // open: clr
  Register #(.width(1)) register_6 (.D(out_16), .en(IR_in), .Q(register_1_q[5]), .clk(nand_1_out));  // open: clr
  Register #(.width(1)) register_7 (.D(out_15), .en(IR_in), .Q(register_1_q[6]), .clk(nand_1_out));  // open: clr
  Register #(.width(1)) register_8 (.D(out_14), .en(IR_in), .Q(register_1_q[7]), .clk(nand_1_out));  // open: clr
  Register #(.width(1)) register_9 (.D(out_13), .en(IR_in), .Q(register_1_q[8]), .clk(nand_1_out));  // open: clr
  Register #(.width(1)) register_10 (.D(out_12), .en(IR_in), .Q(register_1_q[9]), .clk(nand_1_out));  // open: clr
  Register #(.width(1)) register_11 (.D(out_11), .en(IR_in), .Q(register_1_q[10]), .clk(nand_1_out));  // open: clr
  Register #(.width(1)) register_12 (.D(out_10), .en(IR_in), .Q(register_1_q[11]), .clk(nand_1_out));  // open: clr
  not not_2 (not_2_out, register_1_q[0]);
  and and_2 (and_2_out, register_1_q[0], register_1_q[1]);
  and and_3 (and_3_out, and_2_out, register_1_q[2]);
  or or_1 (or_1_out, button_1_out, Reset_Counter);
  xor xor_1 (xor_1_out, register_1_q[0], register_1_q[1]);
  xor xor_2 (xor_2_out, and_2_out, register_1_q[2]);
  xor xor_3 (xor_3_out, and_3_out, register_1_q[3]);
  Button button_1 (.out(button_1_out));
  Register #(.width(1)) register_13 (.D(out_17), .en(C_in), .Q(register_13_q), .clk(nand_1_out));  // open: clr
  Register #(.width(1)) register_14 (.D(out_16), .en(C_in), .Q(register_14_q), .clk(nand_1_out));  // open: clr
  Register #(.width(1)) register_15 (.D(out_15), .en(C_in), .Q(register_15_q), .clk(nand_1_out));  // open: clr
  Register #(.width(1)) register_16 (.D(out_14), .en(C_in), .Q(register_16_q), .clk(nand_1_out));  // open: clr
  Register #(.width(1)) register_17 (.D(out_13), .en(C_in), .Q(register_17_q), .clk(nand_1_out));  // open: clr
  Register #(.width(1)) register_18 (.D(out_12), .en(C_in), .Q(register_18_q), .clk(nand_1_out));  // open: clr
  Register #(.width(1)) register_19 (.D(out_11), .en(C_in), .Q(register_19_q), .clk(nand_1_out));  // open: clr
  Register #(.width(1)) register_20 (.D(out_10), .en(C_in), .Q(register_20_q), .clk(nand_1_out));  // open: clr
  and and_4 (and_4_out, C_out, register_13_q);
  and and_5 (and_5_out, C_out, register_14_q);
  and and_6 (and_6_out, C_out, register_15_q);
  and and_7 (and_7_out, C_out, register_16_q);
  and and_8 (and_8_out, C_out, register_17_q);
  and and_9 (and_9_out, C_out, register_18_q);
  and and_10 (and_10_out, C_out, register_19_q);
  and and_11 (and_11_out, C_out, register_20_q);
  ROM #(.addrWidth(14)) rom_1 (
    .addr({2'b00, register_1_q}),
    .data({PCH_in, PCL_in, PCH_write, PCL_write, IR_in, MEM_out, Reset_Counter, HLT}));  // open: sel
  ROM #(.addrWidth(14)) rom_2 (
    .addr({2'b01, register_1_q}), .data({B_out, B_in, A_out, A_in, RAM_out, RAM_in, MARH_in, MARL_in}));  // open: sel
  ROM #(.addrWidth(14)) rom_3 (
    .addr({2'b10, register_1_q}), .data({JZH, JZL, OUT_in, SIGNED_in, SIGNED_data, ALU_op1, ALU_op0, ALU_out}));  // open: sel
  ROM #(.addrWidth(14)) rom_4 (
    .addr({2'b11, register_1_q}), .data({rom_4_data, JCH, JCL, PCH_out, PCL_out, C_out, C_in}));  // open: sel
  or or_2 (or_2_out, or_26_out, or_27_out);
  or or_3 (out_17, or_2_out, or_4_out);
  or or_4 (or_4_out, or_28_out, or_29_out);
  or or_5 (or_5_out, or_30_out, or_31_out);
  or or_6 (out_16, or_5_out, or_7_out);
  or or_7 (or_7_out, or_32_out, or_33_out);
  or or_8 (or_8_out, or_34_out, or_35_out);
  or or_9 (out_15, or_8_out, or_10_out);
  or or_10 (or_10_out, or_36_out, or_37_out);
  or or_11 (or_11_out, or_38_out, or_39_out);
  or or_12 (out_14, or_11_out, or_13_out);
  or or_13 (or_13_out, or_40_out, or_41_out);
  or or_14 (or_14_out, or_42_out, or_43_out);
  or or_15 (out_13, or_14_out, or_16_out);
  or or_16 (or_16_out, or_44_out, or_45_out);
  or or_17 (or_17_out, or_46_out, or_47_out);
  or or_18 (out_12, or_17_out, or_19_out);
  or or_19 (or_19_out, or_48_out, or_49_out);
  or or_20 (or_20_out, or_50_out, or_51_out);
  or or_21 (out_11, or_20_out, or_22_out);
  or or_22 (or_22_out, or_52_out, or_53_out);
  or or_23 (or_23_out, or_54_out, or_55_out);
  or or_24 (out_10, or_23_out, or_25_out);
  or or_25 (or_25_out, or_56_out, or_57_out);
  Register #(.width(1)) register_21 (.D(out_17), .en(MARL_in), .Q(register_21_q[0]), .clk(nand_1_out));  // open: clr
  Register #(.width(1)) register_22 (.D(out_16), .en(MARL_in), .Q(register_21_q[1]), .clk(nand_1_out));  // open: clr
  Register #(.width(1)) register_23 (.D(out_15), .en(MARL_in), .Q(register_21_q[2]), .clk(nand_1_out));  // open: clr
  Register #(.width(1)) register_24 (.D(out_14), .en(MARL_in), .Q(register_21_q[3]), .clk(nand_1_out));  // open: clr
  Register #(.width(1)) register_25 (.D(out_13), .en(MARL_in), .Q(register_21_q[4]), .clk(nand_1_out));  // open: clr
  Register #(.width(1)) register_26 (.D(out_12), .en(MARL_in), .Q(register_21_q[5]), .clk(nand_1_out));  // open: clr
  Register #(.width(1)) register_27 (.D(out_11), .en(MARL_in), .Q(register_21_q[6]), .clk(nand_1_out));  // open: clr
  Register #(.width(1)) register_28 (.D(out_10), .en(MARL_in), .Q(register_21_q[7]), .clk(nand_1_out));  // open: clr
  Register #(.width(1)) register_29 (.D(out_17), .en(MARH_in), .Q(register_21_q[8]), .clk(nand_1_out));  // open: clr
  Register #(.width(1)) register_30 (.D(out_16), .en(MARH_in), .Q(register_21_q[9]), .clk(nand_1_out));  // open: clr
  Register #(.width(1)) register_31 (.D(out_15), .en(MARH_in), .Q(register_21_q[10]), .clk(nand_1_out));  // open: clr
  Register #(.width(1)) register_32 (.D(out_14), .en(MARH_in), .Q(register_21_q[11]), .clk(nand_1_out));  // open: clr
  Register #(.width(1)) register_33 (.D(out_13), .en(MARH_in), .Q(register_21_q[12]), .clk(nand_1_out));  // open: clr
  Register #(.width(1)) register_34 (.D(out_12), .en(MARH_in), .Q(register_21_q[13]), .clk(nand_1_out));  // open: clr
  Register #(.width(1)) register_35 (.D(out_11), .en(MARH_in), .Q(register_21_q[14]), .clk(nand_1_out));  // open: clr
  Register #(.width(1)) register_36 (.D(out_10), .en(MARH_in), .Q(register_21_q[15]), .clk(nand_1_out));  // open: clr
  Register #(.width(1)) register_37 (.D(out_17), .en(A_in), .Q(register_37_q), .clk(nand_1_out));  // open: clr
  Register #(.width(1)) register_38 (.D(out_16), .en(A_in), .Q(register_38_q), .clk(nand_1_out));  // open: clr
  Register #(.width(1)) register_39 (.D(out_15), .en(A_in), .Q(register_39_q), .clk(nand_1_out));  // open: clr
  Register #(.width(1)) register_40 (.D(out_14), .en(A_in), .Q(register_40_q), .clk(nand_1_out));  // open: clr
  Register #(.width(1)) register_41 (.D(out_13), .en(A_in), .Q(register_41_q), .clk(nand_1_out));  // open: clr
  Register #(.width(1)) register_42 (.D(out_12), .en(A_in), .Q(register_42_q), .clk(nand_1_out));  // open: clr
  Register #(.width(1)) register_43 (.D(out_11), .en(A_in), .Q(register_43_q), .clk(nand_1_out));  // open: clr
  Register #(.width(1)) register_44 (.D(out_10), .en(A_in), .Q(register_44_q), .clk(nand_1_out));  // open: clr
  Register #(.width(1)) register_45 (.D(out_17), .en(B_in), .Q(register_45_q), .clk(nand_1_out));  // open: clr
  Register #(.width(1)) register_46 (.D(out_16), .en(B_in), .Q(register_46_q), .clk(nand_1_out));  // open: clr
  Register #(.width(1)) register_47 (.D(out_15), .en(B_in), .Q(register_47_q), .clk(nand_1_out));  // open: clr
  Register #(.width(1)) register_48 (.D(out_14), .en(B_in), .Q(register_48_q), .clk(nand_1_out));  // open: clr
  Register #(.width(1)) register_49 (.D(out_13), .en(B_in), .Q(register_49_q), .clk(nand_1_out));  // open: clr
  Register #(.width(1)) register_50 (.D(out_12), .en(B_in), .Q(register_50_q), .clk(nand_1_out));  // open: clr
  Register #(.width(1)) register_51 (.D(out_11), .en(B_in), .Q(register_51_q), .clk(nand_1_out));  // open: clr
  Register #(.width(1)) register_52 (.D(out_10), .en(B_in), .Q(register_52_q), .clk(nand_1_out));  // open: clr
  or or_26 (or_26_out, and_103_out, and_33_out);
  or or_27 (or_27_out, and_41_out, and_49_out);
  or or_28 (or_28_out, and_4_out, or_123_out);
  or or_29 (or_29_out, and_70_out, in_9);
  or or_30 (or_30_out, and_104_out, and_34_out);
  or or_31 (or_31_out, and_42_out, and_50_out);
  or or_32 (or_32_out, and_5_out, or_124_out);
  or or_33 (or_33_out, and_82_out, in_8);
  or or_34 (or_34_out, and_105_out, and_35_out);
  or or_35 (or_35_out, and_43_out, and_51_out);
  or or_36 (or_36_out, and_6_out, or_125_out);
  or or_37 (or_37_out, and_91_out, in_7);
  or or_38 (or_38_out, and_106_out, and_36_out);
  or or_39 (or_39_out, and_44_out, and_52_out);
  or or_40 (or_40_out, and_7_out, or_126_out);
  or or_41 (or_41_out, and_98_out, in_6);
  or or_42 (or_42_out, and_107_out, and_37_out);
  or or_43 (or_43_out, and_45_out, and_53_out);
  or or_44 (or_44_out, and_8_out, or_127_out);
  or or_45 (or_45_out, and_111_out, in_5);
  or or_46 (or_46_out, and_108_out, and_38_out);
  or or_47 (or_47_out, and_46_out, and_54_out);
  or or_48 (or_48_out, and_9_out, or_128_out);
  or or_49 (or_49_out, and_116_out, in_4);
  or or_50 (or_50_out, and_109_out, and_39_out);
  or or_51 (or_51_out, and_47_out, and_55_out);
  or or_52 (or_52_out, and_10_out, or_130_out);
  or or_53 (or_53_out, and_121_out, in_3);
  or or_54 (or_54_out, and_110_out, and_40_out);
  or or_55 (or_55_out, and_48_out, and_56_out);
  or or_56 (or_56_out, and_11_out, or_129_out);
  or or_57 (or_57_out, and_126_out, in_2);
  RAM #(.addrWidth(16), .bus("separate")) ram_1 (
    .addr(register_21_q), .din({out_10, out_11, out_12, out_13, out_14, out_15, out_16, out_17}),
    .data(ram_1_data), .str(RAM_in), .clk(nand_1_out));  // open: sel, ld, clr
  not not_3 (not_3_out, ALU_op1);
  not not_4 (not_4_out, register_45_q);
  not not_5 (not_5_out, register_46_q);
  not not_6 (not_6_out, register_47_q);
  not not_7 (not_7_out, register_48_q);
  not not_8 (not_8_out, register_49_q);
  not not_9 (not_9_out, register_50_q);
  not not_10 (not_10_out, register_51_q);
  not not_11 (not_11_out, register_52_q);
  not not_12 (not_12_out, ALU_op0);
  xor xor_4 (xor_4_out, register_37_q, register_45_q);
  and and_12 (and_12_out, register_37_q, register_45_q);
  xor xor_5 (xor_5_out, register_38_q, register_46_q);
  and and_13 (and_13_out, and_12_out, xor_5_out);
  and and_14 (and_14_out, register_38_q, register_46_q);
  xor xor_6 (xor_6_out, register_39_q, register_47_q);
  and and_15 (and_15_out, or_58_out, xor_6_out);
  and and_16 (and_16_out, register_39_q, register_47_q);
  xor xor_7 (xor_7_out, register_40_q, register_48_q);
  and and_17 (and_17_out, or_59_out, xor_7_out);
  and and_18 (and_18_out, register_40_q, register_48_q);
  xor xor_8 (xor_8_out, register_41_q, register_49_q);
  and and_19 (and_19_out, or_60_out, xor_8_out);
  and and_20 (and_20_out, register_41_q, register_49_q);
  xor xor_9 (xor_9_out, register_42_q, register_50_q);
  and and_21 (and_21_out, or_61_out, xor_9_out);
  and and_22 (and_22_out, register_42_q, register_50_q);
  xor xor_10 (xor_10_out, register_43_q, register_51_q);
  and and_23 (and_23_out, or_62_out, xor_10_out);
  and and_24 (and_24_out, register_43_q, register_51_q);
  xor xor_11 (xor_11_out, register_44_q, register_52_q);
  and and_25 (and_25_out, or_63_out, xor_11_out);
  and and_26 (and_26_out, register_44_q, register_52_q);
  not not_13 (not_13_out, not_4_out);
  xor xor_12 (xor_12_out, not_4_out, not_5_out);
  and and_27 (and_27_out, not_4_out, not_5_out);
  xor xor_13 (xor_13_out, and_27_out, not_6_out);
  and and_28 (and_28_out, and_27_out, not_6_out);
  xor xor_14 (xor_14_out, and_28_out, not_7_out);
  and and_29 (and_29_out, and_28_out, not_7_out);
  xor xor_15 (xor_15_out, and_29_out, not_8_out);
  and and_30 (and_30_out, and_29_out, not_8_out);
  xor xor_16 (xor_16_out, and_30_out, not_9_out);
  and and_31 (and_31_out, and_30_out, not_9_out);
  xor xor_17 (xor_17_out, and_31_out, not_10_out);
  and and_32 (and_32_out, and_31_out, not_10_out);
  xor xor_18 (xor_18_out, and_32_out, not_11_out);
  and and_33 (and_33_out, ram_1_data[0], RAM_out);
  and and_34 (and_34_out, ram_1_data[1], RAM_out);
  and and_35 (and_35_out, ram_1_data[2], RAM_out);
  and and_36 (and_36_out, ram_1_data[3], RAM_out);
  and and_37 (and_37_out, ram_1_data[4], RAM_out);
  and and_38 (and_38_out, ram_1_data[5], RAM_out);
  and and_39 (and_39_out, ram_1_data[6], RAM_out);
  and and_40 (and_40_out, ram_1_data[7], RAM_out);
  and and_41 (and_41_out, register_37_q, A_out);
  and and_42 (and_42_out, register_38_q, A_out);
  and and_43 (and_43_out, register_39_q, A_out);
  and and_44 (and_44_out, register_40_q, A_out);
  and and_45 (and_45_out, register_41_q, A_out);
  and and_46 (and_46_out, register_42_q, A_out);
  and and_47 (and_47_out, register_43_q, A_out);
  and and_48 (and_48_out, register_44_q, A_out);
  and and_49 (and_49_out, register_45_q, B_out);
  and and_50 (and_50_out, register_46_q, B_out);
  and and_51 (and_51_out, register_47_q, B_out);
  and and_52 (and_52_out, register_48_q, B_out);
  and and_53 (and_53_out, register_49_q, B_out);
  and and_54 (and_54_out, register_50_q, B_out);
  and and_55 (and_55_out, register_51_q, B_out);
  and and_56 (and_56_out, register_52_q, B_out);
  and and_57 (and_57_out, and_58_out, xor_4_out);
  and and_58 (and_58_out, not_12_out, not_3_out);
  and and_59 (and_59_out, ALU_op0, not_3_out);
  and and_60 (and_60_out, not_12_out, ALU_op1);
  and and_61 (and_61_out, ALU_op0, ALU_op1);
  xor xor_19 (xor_19_out, and_12_out, xor_5_out);
  or or_58 (or_58_out, and_13_out, and_14_out);
  xor xor_20 (xor_20_out, or_58_out, xor_6_out);
  or or_59 (or_59_out, and_15_out, and_16_out);
  xor xor_21 (xor_21_out, or_59_out, xor_7_out);
  or or_60 (or_60_out, and_17_out, and_18_out);
  xor xor_22 (xor_22_out, or_60_out, xor_8_out);
  or or_61 (or_61_out, and_19_out, and_20_out);
  xor xor_23 (xor_23_out, or_61_out, xor_9_out);
  or or_62 (or_62_out, and_21_out, and_22_out);
  xor xor_24 (xor_24_out, or_62_out, xor_10_out);
  or or_63 (or_63_out, and_23_out, and_24_out);
  xor xor_25 (xor_25_out, or_63_out, xor_11_out);
  or or_64 (or_64_out, and_25_out, and_26_out);
  xor xor_26 (xor_26_out, register_37_q, not_13_out);
  and and_62 (and_62_out, register_37_q, not_13_out);
  xor xor_27 (xor_27_out, register_38_q, xor_12_out);
  and and_63 (and_63_out, register_38_q, xor_12_out);
  xor xor_28 (xor_28_out, register_39_q, xor_13_out);
  and and_64 (and_64_out, register_39_q, xor_13_out);
  xor xor_29 (xor_29_out, register_40_q, xor_14_out);
  and and_65 (and_65_out, register_40_q, xor_14_out);
  xor xor_30 (xor_30_out, register_41_q, xor_15_out);
  and and_66 (and_66_out, register_41_q, xor_15_out);
  xor xor_31 (xor_31_out, register_42_q, xor_16_out);
  and and_67 (and_67_out, register_42_q, xor_16_out);
  xor xor_32 (xor_32_out, register_43_q, xor_17_out);
  and and_68 (and_68_out, register_43_q, xor_17_out);
  xor xor_33 (xor_33_out, register_44_q, xor_18_out);
  and and_69 (and_69_out, register_44_q, xor_18_out);
  and and_70 (and_70_out, or_65_out, ALU_out);
  or or_65 (or_65_out, or_66_out, or_74_out);
  or or_66 (or_66_out, and_57_out, and_71_out);
  and and_71 (and_71_out, and_59_out, xor_26_out);
  and and_72 (and_72_out, and_60_out, register_37_q);
  xor xor_34 (xor_34_out, and_62_out, xor_27_out);
  and and_73 (and_73_out, and_62_out, xor_27_out);
  or or_67 (or_67_out, and_73_out, and_63_out);
  xor xor_35 (xor_35_out, or_67_out, xor_28_out);
  and and_74 (and_74_out, or_67_out, xor_28_out);
  or or_68 (or_68_out, and_74_out, and_64_out);
  xor xor_36 (xor_36_out, or_68_out, xor_29_out);
  and and_75 (and_75_out, or_68_out, xor_29_out);
  or or_69 (or_69_out, and_75_out, and_65_out);
  xor xor_37 (xor_37_out, or_69_out, xor_30_out);
  and and_76 (and_76_out, or_69_out, xor_30_out);
  or or_70 (or_70_out, and_76_out, and_66_out);
  xor xor_38 (xor_38_out, or_70_out, xor_31_out);
  and and_77 (and_77_out, or_70_out, xor_31_out);
  or or_71 (or_71_out, and_77_out, and_67_out);
  xor xor_39 (xor_39_out, or_71_out, xor_32_out);
  and and_78 (and_78_out, or_71_out, xor_32_out);
  or or_72 (or_72_out, and_78_out, and_68_out);
  xor xor_40 (xor_40_out, or_72_out, xor_33_out);
  and and_79 (and_79_out, or_72_out, xor_33_out);
  or or_73 (or_73_out, and_79_out, and_69_out);
  or or_74 (or_74_out, and_72_out, and_80_out);
  and and_80 (and_80_out, and_61_out, nand_2_out);
  and and_81 (and_81_out, and_58_out, xor_19_out);
  nand nand_2 (nand_2_out, register_44_q, register_52_q);
  not not_14 (not_14_out, or_73_out);
  and and_82 (and_82_out, or_75_out, ALU_out);
  or or_75 (or_75_out, or_76_out, or_78_out);
  or or_76 (or_76_out, and_81_out, and_84_out);
  and and_83 (and_83_out, and_60_out, register_44_q);
  and and_84 (and_84_out, and_59_out, xor_34_out);
  and and_85 (and_85_out, and_59_out, not_14_out);
  or or_77 (or_77_out, and_85_out, and_86_out);
  and and_86 (and_86_out, and_58_out, or_64_out);
  or or_78 (or_78_out, and_83_out, and_88_out);
  and and_87 (and_87_out, and_58_out, xor_20_out);
  and and_88 (and_88_out, and_61_out, nand_3_out);
  nand nand_3 (nand_3_out, register_43_q, register_51_q);
  Register #(.width(1)) register_53 (.D(or_77_out), .en(ALU_out), .Q(register_53_q), .clk(nand_1_out));  // open: clr
  and and_89 (and_89_out, JZL, not_30_out);
  and and_90 (and_90_out, JZH, not_30_out);
  and and_91 (and_91_out, or_79_out, ALU_out);
  or or_79 (or_79_out, or_80_out, or_83_out);
  or or_80 (or_80_out, and_87_out, and_92_out);
  and and_92 (and_92_out, and_59_out, xor_35_out);
  and and_93 (and_93_out, and_60_out, register_43_q);
  or or_81 (or_81_out, PCL_in, and_89_out);
  or or_82 (or_82_out, PCH_in, and_90_out);
  or or_83 (or_83_out, and_93_out, and_95_out);
  and and_94 (and_94_out, and_58_out, xor_21_out);
  and and_95 (and_95_out, and_61_out, nand_4_out);
  nand nand_4 (nand_4_out, register_42_q, register_50_q);
  and and_96 (and_96_out, JCL, register_53_q);
  and and_97 (and_97_out, JCH, register_53_q);
  Register #(.width(1)) register_54 (.D(out_17), .en(OUT_in), .Q(register_54_q[0]), .clk(nand_1_out));  // open: clr
  Register #(.width(1)) register_55 (.D(out_16), .en(OUT_in), .Q(register_54_q[1]), .clk(nand_1_out));  // open: clr
  Register #(.width(1)) register_56 (.D(out_15), .en(OUT_in), .Q(register_54_q[2]), .clk(nand_1_out));  // open: clr
  Register #(.width(1)) register_57 (.D(out_14), .en(OUT_in), .Q(register_54_q[3]), .clk(nand_1_out));  // open: clr
  Register #(.width(1)) register_58 (.D(out_13), .en(OUT_in), .Q(register_54_q[4]), .clk(nand_1_out));  // open: clr
  Register #(.width(1)) register_59 (.D(out_12), .en(OUT_in), .Q(register_54_q[5]), .clk(nand_1_out));  // open: clr
  Register #(.width(1)) register_60 (.D(out_11), .en(OUT_in), .Q(register_54_q[6]), .clk(nand_1_out));  // open: clr
  Register #(.width(1)) register_61 (.D(out_10), .en(OUT_in), .Q(register_54_q[7]), .clk(nand_1_out));  // open: clr
  and and_98 (and_98_out, or_84_out, ALU_out);
  or or_84 (or_84_out, or_85_out, or_88_out);
  or or_85 (or_85_out, and_94_out, and_100_out);
  and and_99 (and_99_out, and_60_out, register_42_q);
  and and_100 (and_100_out, and_59_out, xor_36_out);
  or or_86 (or_86_out, or_81_out, and_96_out);
  or or_87 (or_87_out, or_82_out, and_97_out);
  or or_88 (or_88_out, and_99_out, and_102_out);
  and and_101 (and_101_out, and_58_out, xor_22_out);
  and and_102 (and_102_out, and_61_out, nand_5_out);
  nand nand_5 (nand_5_out, register_41_q, register_49_q);
  ROM #(.addrWidth(15)) rom_5 (.addr(register_63_q), .data(rom_5_data));  // open: sel
  and and_103 (and_103_out, MEM_out, rom_5_data[0]);
  and and_104 (and_104_out, MEM_out, rom_5_data[1]);
  and and_105 (and_105_out, MEM_out, rom_5_data[2]);
  and and_106 (and_106_out, MEM_out, rom_5_data[3]);
  and and_107 (and_107_out, MEM_out, rom_5_data[4]);
  and and_108 (and_108_out, MEM_out, rom_5_data[5]);
  and and_109 (and_109_out, MEM_out, rom_5_data[6]);
  and and_110 (and_110_out, MEM_out, rom_5_data[7]);
  and and_111 (and_111_out, or_89_out, ALU_out);
  or or_89 (or_89_out, or_90_out, or_91_out);
  or or_90 (or_90_out, and_101_out, and_112_out);
  and and_112 (and_112_out, and_59_out, xor_37_out);
  and and_113 (and_113_out, and_60_out, register_41_q);
  ROM #(.addrWidth(9)) rom_6 (.addr(register_54_q), .data(rom_6_data));  // open: sel
  ROM #(.addrWidth(9)) rom_7 (.addr(register_54_q), .data(rom_7_data));  // open: sel
  ROM #(.addrWidth(9)) rom_8 (.addr(register_54_q), .data(rom_8_data));  // open: sel
  Register #(.width(1)) register_62 (
    .D(SIGNED_data), .en(SIGNED_in), .Q(register_54_q[8]), .clk(nand_1_out));  // open: clr
  or or_91 (or_91_out, and_113_out, and_115_out);
  and and_114 (and_114_out, and_58_out, xor_23_out);
  and and_115 (and_115_out, and_61_out, nand_6_out);
  nand nand_6 (nand_6_out, register_40_q, register_48_q);
  DotMatrix #(.matrixcols(3), .matrixrows(1)) dotmatrix_1 (
    .col0(rom_6_data[7]), .col1(rom_6_data[7]), .col2(rom_6_data[7]));
  and and_116 (and_116_out, or_92_out, ALU_out);
  or or_92 (or_92_out, or_93_out, or_94_out);
  or or_93 (or_93_out, and_114_out, and_118_out);
  and and_117 (and_117_out, and_60_out, register_40_q);
  and and_118 (and_118_out, and_59_out, xor_38_out);
  _7_Segment_Display u_7_segment_display_1 (
    .g(rom_7_data[3]), .f(rom_7_data[2]), .a(rom_7_data[1]), .b(rom_7_data[0]), .e(rom_7_data[4]),
    .d(rom_7_data[5]), .c(rom_7_data[6]));  // open: dp
  _7_Segment_Display u_7_segment_display_2 (
    .g(rom_6_data[3]), .f(rom_6_data[2]), .a(rom_6_data[1]), .b(rom_6_data[0]), .e(rom_6_data[4]),
    .d(rom_6_data[5]), .c(rom_6_data[6]));  // open: dp
  or or_94 (or_94_out, and_117_out, and_120_out);
  and and_119 (and_119_out, and_58_out, xor_24_out);
  and and_120 (and_120_out, and_61_out, nand_7_out);
  nand nand_7 (nand_7_out, register_39_q, register_47_q);
  _7_Segment_Display u_7_segment_display_3 (
    .g(rom_8_data[3]), .f(rom_8_data[2]), .a(rom_8_data[1]), .b(rom_8_data[0]), .e(rom_8_data[4]),
    .d(rom_8_data[5]), .c(rom_8_data[6]));  // open: dp
  and and_121 (and_121_out, or_95_out, ALU_out);
  or or_95 (or_95_out, or_96_out, or_97_out);
  or or_96 (or_96_out, and_119_out, and_122_out);
  and and_122 (and_122_out, and_59_out, xor_39_out);
  and and_123 (and_123_out, and_60_out, register_39_q);
  or or_97 (or_97_out, and_123_out, and_125_out);
  and and_124 (and_124_out, and_58_out, xor_25_out);
  and and_125 (and_125_out, and_61_out, nand_8_out);
  nand nand_8 (nand_8_out, register_38_q, register_46_q);
  and and_126 (and_126_out, or_98_out, ALU_out);
  or or_98 (or_98_out, or_99_out, or_100_out);
  or or_99 (or_99_out, and_124_out, and_128_out);
  and and_127 (and_127_out, and_60_out, register_38_q);
  and and_128 (and_128_out, and_59_out, xor_40_out);
  or or_100 (or_100_out, and_127_out, and_129_out);
  and and_129 (and_129_out, and_61_out, nand_9_out);
  nand nand_9 (nand_9_out, register_37_q, register_45_q);
  and and_130 (and_130_out, not_31_out, not_15_out);
  not not_15 (not_15_out, PCL_write);
  and and_131 (and_131_out, PCL_write, out_17);
  and and_132 (and_132_out, xor_41_out, not_16_out);
  not not_16 (not_16_out, PCL_write);
  and and_133 (and_133_out, PCL_write, out_16);
  and and_134 (and_134_out, xor_42_out, not_17_out);
  not not_17 (not_17_out, PCL_write);
  and and_135 (and_135_out, PCL_write, out_15);
  and and_136 (and_136_out, xor_43_out, not_18_out);
  not not_18 (not_18_out, PCL_write);
  and and_137 (and_137_out, PCL_write, out_14);
  and and_138 (and_138_out, xor_44_out, not_19_out);
  not not_19 (not_19_out, PCL_write);
  and and_139 (and_139_out, PCL_write, out_13);
  and and_140 (and_140_out, xor_45_out, not_20_out);
  not not_20 (not_20_out, PCL_write);
  and and_141 (and_141_out, PCL_write, out_12);
  and and_142 (and_142_out, xor_46_out, not_21_out);
  not not_21 (not_21_out, PCL_write);
  and and_143 (and_143_out, PCL_write, out_11);
  and and_144 (and_144_out, xor_47_out, not_22_out);
  not not_22 (not_22_out, PCL_write);
  and and_145 (and_145_out, PCL_write, out_10);
  and and_146 (and_146_out, xor_48_out, not_23_out);
  not not_23 (not_23_out, PCH_write);
  and and_147 (and_147_out, PCH_write, out_17);
  and and_148 (and_148_out, xor_49_out, not_24_out);
  not not_24 (not_24_out, PCH_write);
  and and_149 (and_149_out, PCH_write, out_16);
  and and_150 (and_150_out, xor_50_out, not_25_out);
  not not_25 (not_25_out, PCH_write);
  and and_151 (and_151_out, PCH_write, out_15);
  and and_152 (and_152_out, xor_51_out, not_26_out);
  not not_26 (not_26_out, PCH_write);
  and and_153 (and_153_out, PCH_write, out_14);
  and and_154 (and_154_out, xor_52_out, not_27_out);
  not not_27 (not_27_out, PCH_write);
  and and_155 (and_155_out, PCH_write, out_13);
  and and_156 (and_156_out, xor_53_out, not_28_out);
  not not_28 (not_28_out, PCH_write);
  and and_157 (and_157_out, PCH_write, out_12);
  and and_158 (and_158_out, xor_54_out, not_29_out);
  not not_29 (not_29_out, PCH_write);
  and and_159 (and_159_out, PCH_write, out_11);
  or or_101 (or_101_out, or_102_out, or_103_out);
  or or_102 (or_102_out, register_37_q, register_38_q);
  or or_103 (or_103_out, register_39_q, register_40_q);
  or or_104 (or_104_out, and_130_out, and_131_out);
  or or_105 (or_105_out, and_132_out, and_133_out);
  or or_106 (or_106_out, and_134_out, and_135_out);
  or or_107 (or_107_out, and_136_out, and_137_out);
  or or_108 (or_108_out, and_138_out, and_139_out);
  or or_109 (or_109_out, and_140_out, and_141_out);
  or or_110 (or_110_out, and_142_out, and_143_out);
  or or_111 (or_111_out, and_144_out, and_145_out);
  or or_112 (or_112_out, and_146_out, and_147_out);
  or or_113 (or_113_out, and_148_out, and_149_out);
  or or_114 (or_114_out, and_150_out, and_151_out);
  or or_115 (or_115_out, and_152_out, and_153_out);
  or or_116 (or_116_out, and_154_out, and_155_out);
  or or_117 (or_117_out, and_156_out, and_157_out);
  or or_118 (or_118_out, and_158_out, and_159_out);
  not not_30 (not_30_out, or_119_out);
  or or_119 (or_119_out, or_101_out, or_120_out);
  or or_120 (or_120_out, or_121_out, or_122_out);
  or or_121 (or_121_out, register_41_q, register_42_q);
  or or_122 (or_122_out, register_43_q, register_44_q);
  Register #(.width(1)) register_63 (
    .D(or_104_out), .en(or_86_out), .Q(register_63_q[0]), .clk(nand_1_out));  // open: clr
  Register #(.width(1)) register_64 (
    .D(or_105_out), .en(or_86_out), .Q(register_63_q[1]), .clk(nand_1_out));  // open: clr
  Register #(.width(1)) register_65 (
    .D(or_106_out), .en(or_86_out), .Q(register_63_q[2]), .clk(nand_1_out));  // open: clr
  Register #(.width(1)) register_66 (
    .D(or_107_out), .en(or_86_out), .Q(register_63_q[3]), .clk(nand_1_out));  // open: clr
  Register #(.width(1)) register_67 (
    .D(or_108_out), .en(or_86_out), .Q(register_63_q[4]), .clk(nand_1_out));  // open: clr
  Register #(.width(1)) register_68 (
    .D(or_109_out), .en(or_86_out), .Q(register_63_q[5]), .clk(nand_1_out));  // open: clr
  Register #(.width(1)) register_69 (
    .D(or_110_out), .en(or_86_out), .Q(register_63_q[6]), .clk(nand_1_out));  // open: clr
  Register #(.width(1)) register_70 (
    .D(or_111_out), .en(or_86_out), .Q(register_63_q[7]), .clk(nand_1_out));  // open: clr
  Register #(.width(1)) register_71 (
    .D(or_112_out), .en(or_87_out), .Q(register_63_q[8]), .clk(nand_1_out));  // open: clr
  Register #(.width(1)) register_72 (
    .D(or_113_out), .en(or_87_out), .Q(register_63_q[9]), .clk(nand_1_out));  // open: clr
  Register #(.width(1)) register_73 (
    .D(or_114_out), .en(or_87_out), .Q(register_63_q[10]), .clk(nand_1_out));  // open: clr
  Register #(.width(1)) register_74 (
    .D(or_115_out), .en(or_87_out), .Q(register_63_q[11]), .clk(nand_1_out));  // open: clr
  Register #(.width(1)) register_75 (
    .D(or_116_out), .en(or_87_out), .Q(register_63_q[12]), .clk(nand_1_out));  // open: clr
  Register #(.width(1)) register_76 (
    .D(or_117_out), .en(or_87_out), .Q(register_63_q[13]), .clk(nand_1_out));  // open: clr
  Register #(.width(1)) register_77 (
    .D(or_118_out), .en(or_87_out), .Q(register_63_q[14]), .clk(nand_1_out));  // open: clr
  not not_31 (not_31_out, register_63_q[0]);
  xor xor_41 (xor_41_out, register_63_q[0], register_63_q[1]);
  and and_160 (and_160_out, register_63_q[0], register_63_q[1]);
  xor xor_42 (xor_42_out, and_160_out, register_63_q[2]);
  and and_161 (and_161_out, and_160_out, register_63_q[2]);
  xor xor_43 (xor_43_out, and_161_out, register_63_q[3]);
  and and_162 (and_162_out, and_161_out, register_63_q[3]);
  xor xor_44 (xor_44_out, and_162_out, register_63_q[4]);
  and and_163 (and_163_out, and_162_out, register_63_q[4]);
  xor xor_45 (xor_45_out, and_163_out, register_63_q[5]);
  and and_164 (and_164_out, and_163_out, register_63_q[5]);
  xor xor_46 (xor_46_out, and_164_out, register_63_q[6]);
  and and_165 (and_165_out, and_164_out, register_63_q[6]);
  xor xor_47 (xor_47_out, and_165_out, register_63_q[7]);
  and and_166 (and_166_out, and_165_out, register_63_q[7]);
  xor xor_48 (xor_48_out, and_166_out, register_63_q[8]);
  and and_167 (and_167_out, and_166_out, register_63_q[8]);
  xor xor_49 (xor_49_out, and_167_out, register_63_q[9]);
  and and_168 (and_168_out, and_167_out, register_63_q[9]);
  xor xor_50 (xor_50_out, and_168_out, register_63_q[10]);
  and and_169 (and_169_out, and_168_out, register_63_q[10]);
  xor xor_51 (xor_51_out, and_169_out, register_63_q[11]);
  and and_170 (and_170_out, and_169_out, register_63_q[11]);
  xor xor_52 (xor_52_out, and_170_out, register_63_q[12]);
  and and_171 (and_171_out, and_170_out, register_63_q[12]);
  xor xor_53 (xor_53_out, and_171_out, register_63_q[13]);
  and and_172 (and_172_out, and_171_out, register_63_q[13]);
  xor xor_54 (xor_54_out, and_172_out, register_63_q[14]);
  and and_173 (and_173_out, PCH_out, register_63_q[8]);
  or or_123 (or_123_out, and_173_out, and_174_out);
  and and_174 (and_174_out, PCL_out, register_63_q[0]);
  and and_175 (and_175_out, PCH_out, register_63_q[9]);
  or or_124 (or_124_out, and_175_out, and_176_out);
  and and_176 (and_176_out, PCL_out, register_63_q[1]);
  and and_177 (and_177_out, PCH_out, register_63_q[10]);
  or or_125 (or_125_out, and_177_out, and_178_out);
  and and_178 (and_178_out, PCL_out, register_63_q[2]);
  and and_179 (and_179_out, PCH_out, register_63_q[11]);
  or or_126 (or_126_out, and_179_out, and_180_out);
  and and_180 (and_180_out, PCL_out, register_63_q[3]);
  and and_181 (and_181_out, PCH_out, register_63_q[12]);
  or or_127 (or_127_out, and_181_out, and_182_out);
  and and_182 (and_182_out, PCL_out, register_63_q[4]);
  and and_183 (and_183_out, PCH_out, register_63_q[13]);
  or or_128 (or_128_out, and_183_out, and_184_out);
  and and_184 (and_184_out, PCL_out, register_63_q[5]);
  and and_185 (and_185_out, PCH_out, register_63_q[14]);
  or or_129 (or_129_out, and_185_out, and_186_out);
  and and_186 (and_186_out, PCL_out, register_63_q[6]);
  and and_187 (and_187_out, PCH_out, 1'b0);
  or or_130 (or_130_out, and_187_out, and_188_out);
  and and_188 (and_188_out, PCL_out, register_63_q[7]);

  // Notes on the sheet:
  //   contents of rom_1 (hex, n*v repeats v):
  //   c c0 2 13*0 c c0 4 c0 2 11*0 c c0 4 c0 2 11*0 c c0 4 c0 4 c0 2 9*0 c c0 4 c0 4 c0 2 9*0 c c0 0 0 0 2
  //   10*0 c c0 0 0 0 2 10*0 c c0 4 c0 4 c0 2 9*0 c c0 4 c0 4 c0 2 9*0 c c0 0 0 0 2 10*0 c c0 0 0 0 2 10*0
  //   c c0 0 2 12*0 c c0 0 2 12*0 c c0 0 2 12*0 c c0 0 2 12*0 c c0 0 2 12*0 c c0 0 2 12*0 c c0 4 c0 2 11*0
  //   c c0 4 c0 4 c0 2 9*0 c c0 0 0 0 2 10*0 c c0 4 c0 4 c0 2 9*0 c c0 0 0 0 2 10*0 c c0 4 c0 2 11*0 c c0
  //   0 2 12*0 c c0 0 2 12*0 c c0 0 0 0 2 10*0 c c0 4 c0 4 c0 2 9*0 c c0 0 2 12*0 c c0 0 2 12*0 c c0 0 2
  //   12*0 c c0 4 c0 2 11*0 c c0 4 c0 4 c0 0 2 8*0 c c0 0 2 12*0 c c0 4 c0 2 11*0 c c0 4 c0 4 c0 0 2 8*0 c
  //   c0 0 2 12*0 c c0 0 0 2 11*0 c c0 0 0 0 2 10*0 c c0 4*0 2 9*0 c c0 5*0 2 8*0 c c0 6*0 2 7*0 c c0 7*0
  //   2 6*0 c c0 0 2 12*0 c c0 4 c0 2 11*0 c c0 4 c0 4 c0 0 2 8*0 c c0 4 c0 54 a0 2 9*0 c c0 4 c0 14 20 2
  //   9*0 c c0 4 c0 14 20 2 9*0 c c0 0 0 2 11*0 c c0 a0 50 2 11*0 c c0 2 13*0 c c0 2 13*0 c c0 2 13*0 c c0
  //   2 13*0 c c0 2 13*0 c c0 2 13*0 c c0 2 13*0 c c0 2 13*0 c c0 2 13*0 c c0 2 13*0 c c0 2 13*0 c c0 2
  //   13*0 c c0 2 13*0 c c0 2 13*0 c c0 2 13*0 c c0 2 13*0 c c0 2 13*0 c c0 2 13*0 c c0 2 13*0 c c0 2 13*0
  //   c c0 2 13*0 c c0 2 13*0 c c0 2 13*0 c c0 2 13*0 c c0 2 13*0 c c0 2 13*0 c c0 2 13*0 c c0 2 13*0 c c0
  //   2 13*0 c c0 2 13*0 c c0 2 13*0 c c0 2 13*0 c c0 2 13*0 c c0 2 13*0 c c0 2 13*0 c c0 2 13*0 c c0 2
  //   13*0 c c0 2 13*0 c c0 2 13*0 c c0 2 13*0 c c0 2 13*0 c c0 2 13*0 c c0 2 13*0 c c0 2 13*0 c c0 2 13*0
  //   c c0 2 13*0 c c0 2 13*0 c c0 2 13*0 c c0 2 13*0 c c0 2 13*0 c c0 2 13*0 c c0 2 13*0 c c0 2 13*0 c c0
  //   2 13*0 c c0 2 13*0 c c0 2 13*0 c c0 2 13*0 c c0 2 13*0 c c0 2 13*0 c c0 2 13*0 c c0 2 13*0 c c0 2
  //   13*0 c c0 2 13*0 c c0 2 13*0 c c0 2 13*0 c c0 2 13*0 c c0 2 13*0 c c0 2 13*0 c c0 2 13*0 c c0 2 13*0
  //   c c0 2 13*0 c c0 2 13*0 c c0 2 13*0 c c0 2 13*0 c c0 2 13*0 c c0 2 13*0 c c0 2 13*0 c c0 2 13*0 c c0
  //   2 13*0 c c0 2 13*0 c c0 2 13*0 c c0 2 13*0 c c0 2 13*0 c c0 2 13*0 c c0 2 13*0 c c0 2 13*0 c c0 2
  //   13*0 c c0 2 13*0 c c0 2 13*0 c c0 2 13*0 c c0 2 13*0 c c0 2 13*0 c c0 2 13*0 c c0 2 13*0 c c0 2 13*0
  //   c c0 2 13*0 c c0 2 13*0 c c0 2 13*0 c c0 2 13*0 c c0 2 13*0 c c0 2 13*0 c c0 2 13*0 c c0 2 13*0 c c0
  //   2 13*0 c c0 2 13*0 c c0 2 13*0 c c0 2 13*0 c c0 2 13*0 c c0 2 13*0 c c0 2 13*0 c c0 2 13*0 c c0 2
  //   13*0 c c0 2 13*0 c c0 2 13*0 c c0 2 13*0 c c0 2 13*0 c c0 2 13*0 c c0 2 13*0 c c0 2 13*0 c c0 2 13*0
  //   c c0 2 13*0 c c0 2 13*0 c c0 2 13*0 c c0 2 13*0 c c0 2 13*0 c c0 2 13*0 c c0 2 13*0 c c0 2 13*0 c c0
  //   2 13*0 c c0 2 13*0 c c0 2 13*0 c c0 2 13*0 c c0 2 13*0 c c0 2 13*0 c c0 2 13*0 c c0 2 13*0 c c0 2
  //   13*0 c c0 2 13*0 c c0 2 13*0 c c0 2 13*0 c c0 2 13*0 c c0 2 13*0 c c0 2 13*0 c c0 2 13*0 c c0 2 13*0
  //   c c0 2 13*0 c c0 2 13*0 c c0 2 13*0 c c0 2 13*0 c c0 2 13*0 c c0 2 13*0 c c0 2 13*0 c c0 2 13*0 c c0
  //   2 13*0 c c0 2 13*0 c c0 2 13*0 c c0 2 13*0 c c0 2 13*0 c c0 2 13*0 c c0 2 13*0 c c0 2 13*0 c c0 2
  //   13*0 c c0 2 13*0 c c0 2 13*0 c c0 2 13*0 c c0 2 13*0 c c0 2 13*0 c c0 2 13*0 c c0 2 13*0 c c0 2 13*0
  //   c c0 2 13*0 c c0 2 13*0 c c0 2 13*0 c c0 2 13*0 c c0 2 13*0 c c0 2 13*0 c c0 2 13*0 c c0 2 13*0 c c0
  //   2 13*0 c c0 2 13*0 c c0 2 13*0 c c0 2 13*0 c c0 2 13*0 c c0 2 13*0 c c0 2 13*0 c c0 2 13*0 c c0 2
  //   13*0 c c0 2 13*0 c c0 2 13*0 c c0 2 13*0 c c0 2 13*0 c c0 2 13*0 c c0 2 13*0 c c0 2 13*0 c c0 2 13*0
  //   c c0 2 13*0 c c0 2 13*0 c c0 2 13*0 c c0 2 13*0 c c0 2 13*0 c c0 2 13*0 c c0 2 13*0 c c0 2 13*0 c c0
  //   2 13*0 c c0 2 13*0 c c0 1 2 30*0 10 15*0 40 15*0 2 0 1 18 12*0 2 0 1 48 12*0 22 81 18 13*0 22 81 48
  //   13*0 2 0 1 24 12*0 2 0 1 84 12*0 22 81 24 13*0 22 81 84 13*0 90 15*0 60 15*0 20 15*0 80 15*0 10 15*0
  //   40 31*0 2 0 1 8 12*0 22 81 8 13*0 2 0 1 4 12*0 22 81 4 29*0 20 15*0 80 15*0 22 81 8 13*0 2 0 1 8
  //   44*0 10 15*0 40 10 14*0 2 0 1 48 10 11*0 10 15*0 40 10 14*0 2 0 1 48 10 11*0 10 15*0 10 10 14*0 10
  //   10 10 13*0 4*10 12*0 5*10 11*0 6*10 10*0 7*10 9*0 10 15*0 40 10 14*0 2 0 1 48 10 59*0 10 40 14*0 20
  //   80 3662*0 20 15*0 20 15*0 20 17*0 20 16*0 20 12*0 18 15*0 10 15*0 1 16*0 1 18*0 1 11*0 3 16*0 3 18*0
  //   3 11*0 5 15*0 5 5 14*0 5 5 5 13*0 4*5 12*0 5*5 11*0 6*5 10*0 7*5 9*0 7 16*0 7 18*0 7 29*0 40 80 35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
  //   contents of rom_2 (hex, n*v repeats v):
  //   c c0 2 13*0 c c0 4 c0 2 11*0 c c0 4 c0 2 11*0 c c0 4 c0 4 c0 2 9*0 c c0 4 c0 4 c0 2 9*0 c c0 0 0 0 2
  //   10*0 c c0 0 0 0 2 10*0 c c0 4 c0 4 c0 2 9*0 c c0 4 c0 4 c0 2 9*0 c c0 0 0 0 2 10*0 c c0 0 0 0 2 10*0
  //   c c0 0 2 12*0 c c0 0 2 12*0 c c0 0 2 12*0 c c0 0 2 12*0 c c0 0 2 12*0 c c0 0 2 12*0 c c0 4 c0 2 11*0
  //   c c0 4 c0 4 c0 2 9*0 c c0 0 0 0 2 10*0 c c0 4 c0 4 c0 2 9*0 c c0 0 0 0 2 10*0 c c0 4 c0 2 11*0 c c0
  //   0 2 12*0 c c0 0 2 12*0 c c0 0 0 0 2 10*0 c c0 4 c0 4 c0 2 9*0 c c0 0 2 12*0 c c0 0 2 12*0 c c0 0 2
  //   12*0 c c0 4 c0 2 11*0 c c0 4 c0 4 c0 0 2 8*0 c c0 0 2 12*0 c c0 4 c0 2 11*0 c c0 4 c0 4 c0 0 2 8*0 c
  //   c0 0 2 12*0 c c0 0 0 2 11*0 c c0 0 0 0 2 10*0 c c0 4*0 2 9*0 c c0 5*0 2 8*0 c c0 6*0 2 7*0 c c0 7*0
  //   2 6*0 c c0 0 2 12*0 c c0 4 c0 2 11*0 c c0 4 c0 4 c0 0 2 8*0 c c0 4 c0 54 a0 2 9*0 c c0 4 c0 14 20 2
  //   9*0 c c0 4 c0 14 20 2 9*0 c c0 0 0 2 11*0 c c0 a0 50 2 11*0 c c0 2 13*0 c c0 2 13*0 c c0 2 13*0 c c0
  //   2 13*0 c c0 2 13*0 c c0 2 13*0 c c0 2 13*0 c c0 2 13*0 c c0 2 13*0 c c0 2 13*0 c c0 2 13*0 c c0 2
  //   13*0 c c0 2 13*0 c c0 2 13*0 c c0 2 13*0 c c0 2 13*0 c c0 2 13*0 c c0 2 13*0 c c0 2 13*0 c c0 2 13*0
  //   c c0 2 13*0 c c0 2 13*0 c c0 2 13*0 c c0 2 13*0 c c0 2 13*0 c c0 2 13*0 c c0 2 13*0 c c0 2 13*0 c c0
  //   2 13*0 c c0 2 13*0 c c0 2 13*0 c c0 2 13*0 c c0 2 13*0 c c0 2 13*0 c c0 2 13*0 c c0 2 13*0 c c0 2
  //   13*0 c c0 2 13*0 c c0 2 13*0 c c0 2 13*0 c c0 2 13*0 c c0 2 13*0 c c0 2 13*0 c c0 2 13*0 c c0 2 13*0
  //   c c0 2 13*0 c c0 2 13*0 c c0 2 13*0 c c0 2 13*0 c c0 2 13*0 c c0 2 13*0 c c0 2 13*0 c c0 2 13*0 c c0
  //   2 13*0 c c0 2 13*0 c c0 2 13*0 c c0 2 13*0 c c0 2 13*0 c c0 2 13*0 c c0 2 13*0 c c0 2 13*0 c c0 2
  //   13*0 c c0 2 13*0 c c0 2 13*0 c c0 2 13*0 c c0 2 13*0 c c0 2 13*0 c c0 2 13*0 c c0 2 13*0 c c0 2 13*0
  //   c c0 2 13*0 c c0 2 13*0 c c0 2 13*0 c c0 2 13*0 c c0 2 13*0 c c0 2 13*0 c c0 2 13*0 c c0 2 13*0 c c0
  //   2 13*0 c c0 2 13*0 c c0 2 13*0 c c0 2 13*0 c c0 2 13*0 c c0 2 13*0 c c0 2 13*0 c c0 2 13*0 c c0 2
  //   13*0 c c0 2 13*0 c c0 2 13*0 c c0 2 13*0 c c0 2 13*0 c c0 2 13*0 c c0 2 13*0 c c0 2 13*0 c c0 2 13*0
  //   c c0 2 13*0 c c0 2 13*0 c c0 2 13*0 c c0 2 13*0 c c0 2 13*0 c c0 2 13*0 c c0 2 13*0 c c0 2 13*0 c c0
  //   2 13*0 c c0 2 13*0 c c0 2 13*0 c c0 2 13*0 c c0 2 13*0 c c0 2 13*0 c c0 2 13*0 c c0 2 13*0 c c0 2
  //   13*0 c c0 2 13*0 c c0 2 13*0 c c0 2 13*0 c c0 2 13*0 c c0 2 13*0 c c0 2 13*0 c c0 2 13*0 c c0 2 13*0
  //   c c0 2 13*0 c c0 2 13*0 c c0 2 13*0 c c0 2 13*0 c c0 2 13*0 c c0 2 13*0 c c0 2 13*0 c c0 2 13*0 c c0
  //   2 13*0 c c0 2 13*0 c c0 2 13*0 c c0 2 13*0 c c0 2 13*0 c c0 2 13*0 c c0 2 13*0 c c0 2 13*0 c c0 2
  //   13*0 c c0 2 13*0 c c0 2 13*0 c c0 2 13*0 c c0 2 13*0 c c0 2 13*0 c c0 2 13*0 c c0 2 13*0 c c0 2 13*0
  //   c c0 2 13*0 c c0 2 13*0 c c0 2 13*0 c c0 2 13*0 c c0 2 13*0 c c0 2 13*0 c c0 2 13*0 c c0 2 13*0 c c0
  //   2 13*0 c c0 2 13*0 c c0 2 13*0 c c0 2 13*0 c c0 2 13*0 c c0 2 13*0 c c0 2 13*0 c c0 2 13*0 c c0 2
  //   13*0 c c0 2 13*0 c c0 2 13*0 c c0 2 13*0 c c0 2 13*0 c c0 2 13*0 c c0 2 13*0 c c0 2 13*0 c c0 2 13*0
  //   c c0 2 13*0 c c0 2 13*0 c c0 2 13*0 c c0 2 13*0 c c0 2 13*0 c c0 2 13*0 c c0 2 13*0 c c0 2 13*0 c c0
  //   2 13*0 c c0 2 13*0 c c0 2 13*0 c c0 2 13*0 c c0 2 13*0 c c0 2 13*0 c c0 2 13*0 c c0 2 13*0 c c0 2
  //   13*0 c c0 2 13*0 c c0 2 13*0 c c0 2 13*0 c c0 2 13*0 c c0 2 13*0 c c0 2 13*0 c c0 2 13*0 c c0 2 13*0
  //   c c0 2 13*0 c c0 2 13*0 c c0 2 13*0 c c0 2 13*0 c c0 2 13*0 c c0 2 13*0 c c0 2 13*0 c c0 2 13*0 c c0
  //   2 13*0 c c0 2 13*0 c c0 1 2 30*0 10 15*0 40 15*0 2 0 1 18 12*0 2 0 1 48 12*0 22 81 18 13*0 22 81 48
  //   13*0 2 0 1 24 12*0 2 0 1 84 12*0 22 81 24 13*0 22 81 84 13*0 90 15*0 60 15*0 20 15*0 80 15*0 10 15*0
  //   40 31*0 2 0 1 8 12*0 22 81 8 13*0 2 0 1 4 12*0 22 81 4 29*0 20 15*0 80 15*0 22 81 8 13*0 2 0 1 8
  //   44*0 10 15*0 40 10 14*0 2 0 1 48 10 11*0 10 15*0 40 10 14*0 2 0 1 48 10 11*0 10 15*0 10 10 14*0 10
  //   10 10 13*0 4*10 12*0 5*10 11*0 6*10 10*0 7*10 9*0 10 15*0 40 10 14*0 2 0 1 48 10 59*0 10 40 14*0 20
  //   80 3662*0 20 15*0 20 15*0 20 17*0 20 16*0 20 12*0 18 15*0 10 15*0 1 16*0 1 18*0 1 11*0 3 16*0 3 18*0
  //   3 11*0 5 15*0 5 5 14*0 5 5 5 13*0 4*5 12*0 5*5 11*0 6*5 10*0 7*5 9*0 7 16*0 7 18*0 7 29*0 40 80 35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
  //   contents of rom_3 (hex, n*v repeats v):
  //   c c0 2 13*0 c c0 4 c0 2 11*0 c c0 4 c0 2 11*0 c c0 4 c0 4 c0 2 9*0 c c0 4 c0 4 c0 2 9*0 c c0 0 0 0 2
  //   10*0 c c0 0 0 0 2 10*0 c c0 4 c0 4 c0 2 9*0 c c0 4 c0 4 c0 2 9*0 c c0 0 0 0 2 10*0 c c0 0 0 0 2 10*0
  //   c c0 0 2 12*0 c c0 0 2 12*0 c c0 0 2 12*0 c c0 0 2 12*0 c c0 0 2 12*0 c c0 0 2 12*0 c c0 4 c0 2 11*0
  //   c c0 4 c0 4 c0 2 9*0 c c0 0 0 0 2 10*0 c c0 4 c0 4 c0 2 9*0 c c0 0 0 0 2 10*0 c c0 4 c0 2 11*0 c c0
  //   0 2 12*0 c c0 0 2 12*0 c c0 0 0 0 2 10*0 c c0 4 c0 4 c0 2 9*0 c c0 0 2 12*0 c c0 0 2 12*0 c c0 0 2
  //   12*0 c c0 4 c0 2 11*0 c c0 4 c0 4 c0 0 2 8*0 c c0 0 2 12*0 c c0 4 c0 2 11*0 c c0 4 c0 4 c0 0 2 8*0 c
  //   c0 0 2 12*0 c c0 0 0 2 11*0 c c0 0 0 0 2 10*0 c c0 4*0 2 9*0 c c0 5*0 2 8*0 c c0 6*0 2 7*0 c c0 7*0
  //   2 6*0 c c0 0 2 12*0 c c0 4 c0 2 11*0 c c0 4 c0 4 c0 0 2 8*0 c c0 4 c0 54 a0 2 9*0 c c0 4 c0 14 20 2
  //   9*0 c c0 4 c0 14 20 2 9*0 c c0 0 0 2 11*0 c c0 a0 50 2 11*0 c c0 2 13*0 c c0 2 13*0 c c0 2 13*0 c c0
  //   2 13*0 c c0 2 13*0 c c0 2 13*0 c c0 2 13*0 c c0 2 13*0 c c0 2 13*0 c c0 2 13*0 c c0 2 13*0 c c0 2
  //   13*0 c c0 2 13*0 c c0 2 13*0 c c0 2 13*0 c c0 2 13*0 c c0 2 13*0 c c0 2 13*0 c c0 2 13*0 c c0 2 13*0
  //   c c0 2 13*0 c c0 2 13*0 c c0 2 13*0 c c0 2 13*0 c c0 2 13*0 c c0 2 13*0 c c0 2 13*0 c c0 2 13*0 c c0
  //   2 13*0 c c0 2 13*0 c c0 2 13*0 c c0 2 13*0 c c0 2 13*0 c c0 2 13*0 c c0 2 13*0 c c0 2 13*0 c c0 2
  //   13*0 c c0 2 13*0 c c0 2 13*0 c c0 2 13*0 c c0 2 13*0 c c0 2 13*0 c c0 2 13*0 c c0 2 13*0 c c0 2 13*0
  //   c c0 2 13*0 c c0 2 13*0 c c0 2 13*0 c c0 2 13*0 c c0 2 13*0 c c0 2 13*0 c c0 2 13*0 c c0 2 13*0 c c0
  //   2 13*0 c c0 2 13*0 c c0 2 13*0 c c0 2 13*0 c c0 2 13*0 c c0 2 13*0 c c0 2 13*0 c c0 2 13*0 c c0 2
  //   13*0 c c0 2 13*0 c c0 2 13*0 c c0 2 13*0 c c0 2 13*0 c c0 2 13*0 c c0 2 13*0 c c0 2 13*0 c c0 2 13*0
  //   c c0 2 13*0 c c0 2 13*0 c c0 2 13*0 c c0 2 13*0 c c0 2 13*0 c c0 2 13*0 c c0 2 13*0 c c0 2 13*0 c c0
  //   2 13*0 c c0 2 13*0 c c0 2 13*0 c c0 2 13*0 c c0 2 13*0 c c0 2 13*0 c c0 2 13*0 c c0 2 13*0 c c0 2
  //   13*0 c c0 2 13*0 c c0 2 13*0 c c0 2 13*0 c c0 2 13*0 c c0 2 13*0 c c0 2 13*0 c c0 2 13*0 c c0 2 13*0
  //   c c0 2 13*0 c c0 2 13*0 c c0 2 13*0 c c0 2 13*0 c c0 2 13*0 c c0 2 13*0 c c0 2 13*0 c c0 2 13*0 c c0
  //   2 13*0 c c0 2 13*0 c c0 2 13*0 c c0 2 13*0 c c0 2 13*0 c c0 2 13*0 c c0 2 13*0 c c0 2 13*0 c c0 2
  //   13*0 c c0 2 13*0 c c0 2 13*0 c c0 2 13*0 c c0 2 13*0 c c0 2 13*0 c c0 2 13*0 c c0 2 13*0 c c0 2 13*0
  //   c c0 2 13*0 c c0 2 13*0 c c0 2 13*0 c c0 2 13*0 c c0 2 13*0 c c0 2 13*0 c c0 2 13*0 c c0 2 13*0 c c0
  //   2 13*0 c c0 2 13*0 c c0 2 13*0 c c0 2 13*0 c c0 2 13*0 c c0 2 13*0 c c0 2 13*0 c c0 2 13*0 c c0 2
  //   13*0 c c0 2 13*0 c c0 2 13*0 c c0 2 13*0 c c0 2 13*0 c c0 2 13*0 c c0 2 13*0 c c0 2 13*0 c c0 2 13*0
  //   c c0 2 13*0 c c0 2 13*0 c c0 2 13*0 c c0 2 13*0 c c0 2 13*0 c c0 2 13*0 c c0 2 13*0 c c0 2 13*0 c c0
  //   2 13*0 c c0 2 13*0 c c0 2 13*0 c c0 2 13*0 c c0 2 13*0 c c0 2 13*0 c c0 2 13*0 c c0 2 13*0 c c0 2
  //   13*0 c c0 2 13*0 c c0 2 13*0 c c0 2 13*0 c c0 2 13*0 c c0 2 13*0 c c0 2 13*0 c c0 2 13*0 c c0 2 13*0
  //   c c0 2 13*0 c c0 2 13*0 c c0 2 13*0 c c0 2 13*0 c c0 2 13*0 c c0 2 13*0 c c0 2 13*0 c c0 2 13*0 c c0
  //   2 13*0 c c0 2 13*0 c c0 2 13*0 c c0 2 13*0 c c0 2 13*0 c c0 2 13*0 c c0 2 13*0 c c0 2 13*0 c c0 2
  //   13*0 c c0 2 13*0 c c0 2 13*0 c c0 2 13*0 c c0 2 13*0 c c0 2 13*0 c c0 2 13*0 c c0 2 13*0 c c0 2 13*0
  //   c c0 2 13*0 c c0 2 13*0 c c0 2 13*0 c c0 2 13*0 c c0 2 13*0 c c0 2 13*0 c c0 2 13*0 c c0 2 13*0 c c0
  //   2 13*0 c c0 2 13*0 c c0 1 2 30*0 10 15*0 40 15*0 2 0 1 18 12*0 2 0 1 48 12*0 22 81 18 13*0 22 81 48
  //   13*0 2 0 1 24 12*0 2 0 1 84 12*0 22 81 24 13*0 22 81 84 13*0 90 15*0 60 15*0 20 15*0 80 15*0 10 15*0
  //   40 31*0 2 0 1 8 12*0 22 81 8 13*0 2 0 1 4 12*0 22 81 4 29*0 20 15*0 80 15*0 22 81 8 13*0 2 0 1 8
  //   44*0 10 15*0 40 10 14*0 2 0 1 48 10 11*0 10 15*0 40 10 14*0 2 0 1 48 10 11*0 10 15*0 10 10 14*0 10
  //   10 10 13*0 4*10 12*0 5*10 11*0 6*10 10*0 7*10 9*0 10 15*0 40 10 14*0 2 0 1 48 10 59*0 10 40 14*0 20
  //   80 3662*0 20 15*0 20 15*0 20 17*0 20 16*0 20 12*0 18 15*0 10 15*0 1 16*0 1 18*0 1 11*0 3 16*0 3 18*0
  //   3 11*0 5 15*0 5 5 14*0 5 5 5 13*0 4*5 12*0 5*5 11*0 6*5 10*0 7*5 9*0 7 16*0 7 18*0 7 29*0 40 80 35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
  //   contents of rom_4 (hex, n*v repeats v):
  //   c c0 2 13*0 c c0 4 c0 2 11*0 c c0 4 c0 2 11*0 c c0 4 c0 4 c0 2 9*0 c c0 4 c0 4 c0 2 9*0 c c0 0 0 0 2
  //   10*0 c c0 0 0 0 2 10*0 c c0 4 c0 4 c0 2 9*0 c c0 4 c0 4 c0 2 9*0 c c0 0 0 0 2 10*0 c c0 0 0 0 2 10*0
  //   c c0 0 2 12*0 c c0 0 2 12*0 c c0 0 2 12*0 c c0 0 2 12*0 c c0 0 2 12*0 c c0 0 2 12*0 c c0 4 c0 2 11*0
  //   c c0 4 c0 4 c0 2 9*0 c c0 0 0 0 2 10*0 c c0 4 c0 4 c0 2 9*0 c c0 0 0 0 2 10*0 c c0 4 c0 2 11*0 c c0
  //   0 2 12*0 c c0 0 2 12*0 c c0 0 0 0 2 10*0 c c0 4 c0 4 c0 2 9*0 c c0 0 2 12*0 c c0 0 2 12*0 c c0 0 2
  //   12*0 c c0 4 c0 2 11*0 c c0 4 c0 4 c0 0 2 8*0 c c0 0 2 12*0 c c0 4 c0 2 11*0 c c0 4 c0 4 c0 0 2 8*0 c
  //   c0 0 2 12*0 c c0 0 0 2 11*0 c c0 0 0 0 2 10*0 c c0 4*0 2 9*0 c c0 5*0 2 8*0 c c0 6*0 2 7*0 c c0 7*0
  //   2 6*0 c c0 0 2 12*0 c c0 4 c0 2 11*0 c c0 4 c0 4 c0 0 2 8*0 c c0 4 c0 54 a0 2 9*0 c c0 4 c0 14 20 2
  //   9*0 c c0 4 c0 14 20 2 9*0 c c0 0 0 2 11*0 c c0 a0 50 2 11*0 c c0 2 13*0 c c0 2 13*0 c c0 2 13*0 c c0
  //   2 13*0 c c0 2 13*0 c c0 2 13*0 c c0 2 13*0 c c0 2 13*0 c c0 2 13*0 c c0 2 13*0 c c0 2 13*0 c c0 2
  //   13*0 c c0 2 13*0 c c0 2 13*0 c c0 2 13*0 c c0 2 13*0 c c0 2 13*0 c c0 2 13*0 c c0 2 13*0 c c0 2 13*0
  //   c c0 2 13*0 c c0 2 13*0 c c0 2 13*0 c c0 2 13*0 c c0 2 13*0 c c0 2 13*0 c c0 2 13*0 c c0 2 13*0 c c0
  //   2 13*0 c c0 2 13*0 c c0 2 13*0 c c0 2 13*0 c c0 2 13*0 c c0 2 13*0 c c0 2 13*0 c c0 2 13*0 c c0 2
  //   13*0 c c0 2 13*0 c c0 2 13*0 c c0 2 13*0 c c0 2 13*0 c c0 2 13*0 c c0 2 13*0 c c0 2 13*0 c c0 2 13*0
  //   c c0 2 13*0 c c0 2 13*0 c c0 2 13*0 c c0 2 13*0 c c0 2 13*0 c c0 2 13*0 c c0 2 13*0 c c0 2 13*0 c c0
  //   2 13*0 c c0 2 13*0 c c0 2 13*0 c c0 2 13*0 c c0 2 13*0 c c0 2 13*0 c c0 2 13*0 c c0 2 13*0 c c0 2
  //   13*0 c c0 2 13*0 c c0 2 13*0 c c0 2 13*0 c c0 2 13*0 c c0 2 13*0 c c0 2 13*0 c c0 2 13*0 c c0 2 13*0
  //   c c0 2 13*0 c c0 2 13*0 c c0 2 13*0 c c0 2 13*0 c c0 2 13*0 c c0 2 13*0 c c0 2 13*0 c c0 2 13*0 c c0
  //   2 13*0 c c0 2 13*0 c c0 2 13*0 c c0 2 13*0 c c0 2 13*0 c c0 2 13*0 c c0 2 13*0 c c0 2 13*0 c c0 2
  //   13*0 c c0 2 13*0 c c0 2 13*0 c c0 2 13*0 c c0 2 13*0 c c0 2 13*0 c c0 2 13*0 c c0 2 13*0 c c0 2 13*0
  //   c c0 2 13*0 c c0 2 13*0 c c0 2 13*0 c c0 2 13*0 c c0 2 13*0 c c0 2 13*0 c c0 2 13*0 c c0 2 13*0 c c0
  //   2 13*0 c c0 2 13*0 c c0 2 13*0 c c0 2 13*0 c c0 2 13*0 c c0 2 13*0 c c0 2 13*0 c c0 2 13*0 c c0 2
  //   13*0 c c0 2 13*0 c c0 2 13*0 c c0 2 13*0 c c0 2 13*0 c c0 2 13*0 c c0 2 13*0 c c0 2 13*0 c c0 2 13*0
  //   c c0 2 13*0 c c0 2 13*0 c c0 2 13*0 c c0 2 13*0 c c0 2 13*0 c c0 2 13*0 c c0 2 13*0 c c0 2 13*0 c c0
  //   2 13*0 c c0 2 13*0 c c0 2 13*0 c c0 2 13*0 c c0 2 13*0 c c0 2 13*0 c c0 2 13*0 c c0 2 13*0 c c0 2
  //   13*0 c c0 2 13*0 c c0 2 13*0 c c0 2 13*0 c c0 2 13*0 c c0 2 13*0 c c0 2 13*0 c c0 2 13*0 c c0 2 13*0
  //   c c0 2 13*0 c c0 2 13*0 c c0 2 13*0 c c0 2 13*0 c c0 2 13*0 c c0 2 13*0 c c0 2 13*0 c c0 2 13*0 c c0
  //   2 13*0 c c0 2 13*0 c c0 2 13*0 c c0 2 13*0 c c0 2 13*0 c c0 2 13*0 c c0 2 13*0 c c0 2 13*0 c c0 2
  //   13*0 c c0 2 13*0 c c0 2 13*0 c c0 2 13*0 c c0 2 13*0 c c0 2 13*0 c c0 2 13*0 c c0 2 13*0 c c0 2 13*0
  //   c c0 2 13*0 c c0 2 13*0 c c0 2 13*0 c c0 2 13*0 c c0 2 13*0 c c0 2 13*0 c c0 2 13*0 c c0 2 13*0 c c0
  //   2 13*0 c c0 2 13*0 c c0 2 13*0 c c0 2 13*0 c c0 2 13*0 c c0 2 13*0 c c0 2 13*0 c c0 2 13*0 c c0 2
  //   13*0 c c0 2 13*0 c c0 2 13*0 c c0 2 13*0 c c0 2 13*0 c c0 2 13*0 c c0 2 13*0 c c0 2 13*0 c c0 2 13*0
  //   c c0 2 13*0 c c0 2 13*0 c c0 2 13*0 c c0 2 13*0 c c0 2 13*0 c c0 2 13*0 c c0 2 13*0 c c0 2 13*0 c c0
  //   2 13*0 c c0 2 13*0 c c0 1 2 30*0 10 15*0 40 15*0 2 0 1 18 12*0 2 0 1 48 12*0 22 81 18 13*0 22 81 48
  //   13*0 2 0 1 24 12*0 2 0 1 84 12*0 22 81 24 13*0 22 81 84 13*0 90 15*0 60 15*0 20 15*0 80 15*0 10 15*0
  //   40 31*0 2 0 1 8 12*0 22 81 8 13*0 2 0 1 4 12*0 22 81 4 29*0 20 15*0 80 15*0 22 81 8 13*0 2 0 1 8
  //   44*0 10 15*0 40 10 14*0 2 0 1 48 10 11*0 10 15*0 40 10 14*0 2 0 1 48 10 11*0 10 15*0 10 10 14*0 10
  //   10 10 13*0 4*10 12*0 5*10 11*0 6*10 10*0 7*10 9*0 10 15*0 40 10 14*0 2 0 1 48 10 59*0 10 40 14*0 20
  //   80 3662*0 20 15*0 20 15*0 20 17*0 20 16*0 20 12*0 18 15*0 10 15*0 1 16*0 1 18*0 1 11*0 3 16*0 3 18*0
  //   3 11*0 5 15*0 5 5 14*0 5 5 5 13*0 4*5 12*0 5*5 11*0 6*5 10*0 7*5 9*0 7 16*0 7 18*0 7 29*0 40 80 35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
  //   Manual Bus Override
  //   contents of rom_5 (hex, n*v repeats v):
  //   7 ff fd 1 ff 7 ff fc 1 fa 7 ff fb 3 ff fd 1 f1 7 ff fd 1a ff fd 2f 1 1 7 ff fd b d 1e 69 7 ff ff 10
  //   20 2e 0 31 2b 80 c 2a 2e 0 36 1 0 7 ff fd 3 ff fb 2 1 2e 0 41 2d 0 4b 3 ff fc 20 7 ff fc 3 ff fb 20
  //   7 ff fb c 3 ff fc 12 ff ff 15 2f d 2 1 3 ff fd 2e 0 64 f 1d d 3 ff fb 2e 0 6d 2d 0 77 3 ff fc 20 7 f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
  //   contents of rom_6 (hex, n*v repeats v):
  //   100*77 100*41 56*3b 100*77 28*41 29*c1 99*f7
  //   contents of rom_7 (hex, n*v repeats v):
  //   10*77 10*41 10*3b 10*6b 10*4d 10*6e 10*7e 10*43 10*7f 10*6f 10*77 10*41 10*3b 10*6b 10*4d 10*6e
  //   10*7e 10*43 10*7f 10*6f 10*77 10*41 10*3b 10*6b 10*4d 6*6e 10*77 10*41 10*3b 10*6b 10*4d 10*6e 10*7e
  //   10*43 10*7f 10*6f 10*77 10*41 17*3b 10*41 10*77 10*6f 10*7f 10*43 10*7e 10*6e 10*4d 10*6b 10*3b
  //   10*41 9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
  //   contents of rom_8 (hex, n*v repeats v):
  //   77 41 3b 6b 4d 6e 7e 43 7f 6f 77 41 3b 6b 4d 6e 7e 43 7f 6f 77 41 3b 6b 4d 6e 7e 43 7f 6f 77 41 3b
  //   6b 4d 6e 7e 43 7f 6f 77 41 3b 6b 4d 6e 7e 43 7f 6f 77 41 3b 6b 4d 6e 7e 43 7f 6f 77 41 3b 6b 4d 6e
  //   7e 43 7f 6f 77 41 3b 6b 4d 6e 7e 43 7f 6f 77 41 3b 6b 4d 6e 7e 43 7f 6f 77 41 3b 6b 4d 6e 7e 43 7f
  //   6f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
endmodule
